# Fritzing sketch ckt diagram (saved by Fritzing 0.9.3b)

parts:
  Raspberry_Pi_1 = Raspberry Pi 3 [part_number=RPI-3-V1.2]
  CAMERA1 = TTL Serial JPEG Camera  # not connected
  Part1 = Arduino Uno (Rev3) - ICSP
  M1 = bb-usb-cable [package=THT]  # not connected
  M2 = BTS7960
  M3 = BTS7960
  hc-sr1 = hc-sr04
  KY-1 = Keyes Relay [package=THT]
  S1 = Square Pushbutton
  S2 = Square Pushbutton
  Part2 = Solar Panel [package="Renogy 50 Watts 12 Volt Monocrystalline Bendable Solar Panel"]
  BAT1 = 12 battery [package=battery]
  Mod1 = Solar Charge Controller [part_number="KLD Series Solar Charge Controller PWM" package=PWM-Model]

nets:
  N1: Raspberry_Pi_1.GPIO17, hc-sr1.Trig
  N2: Raspberry_Pi_1.GPIO27, hc-sr1.Echo
  N3: Raspberry_Pi_1.GPIO22, KY-1.signal
  GND: Raspberry_Pi_1.GND, hc-sr1.GND, KY-1.ground
  5V: Raspberry_Pi_1.5V, hc-sr1.VCC, KY-1.power
  N4: Part1.ICSP_MISO, Part1.D12/MISO, M2.pin1
  N5: Part1.GND, M2.pin8, M3.pin8, S1.leg1, S2.leg1
  N6: Part1.D8, M3.pin1
  N7: Part1.D9_PWM, M3.pin2
  N8: Part1.D10_PWM/SS, M3.pin3, M3.pin4
  N9: Part1.D11_PWM/MOSI, M2.pin3, M2.pin4
  N10: Part1.D13/SCK, M2.pin2
  N11: Part1.D4, S2.leg0
  N12: Part1.D5_PWM, S1.leg0
  N13: Part1.5V, M2.pin7, M3.pin7
  N14: M2.pin11, M3.pin11, BAT1.+
  N15: M2.pin12, M3.pin12, BAT1.-, Mod1.Connector_4
  N16: Part2.Connector_1, Mod1.Connector_5
  N17: Part2.Connector_2, Mod1.Connector_6

custom parts:
  TTL Serial JPEG Camera: TTL Serial JPEG Camera with NTSC Out
  bb-usb-cable: Breadboard only, no connectors USB cable for the Raspberry PIs.
  BTS7960: BTS7960 43A Peak Power H-Bridge PWM Motor Driver
  Keyes Relay: The Keyes 5V relay module is suitable for SCM development, home appliance control. It uses a 5V~12V TIL control signal which can control DC / AC signal.
  Solar Panel: Renogy 50 Watts 12 Volt Solar Panel
  12 battery: 12V lead acid type battery, like the Husqvarna YTH2448 12V 35AH battery. This is the mini version 1/4 the size of the actual battery to be closer to typical breadboard parts (around 2in wide rathher than 7in). The pads in pcb are sized to accomidate up to 14ga wire (as these batterys will deliver high currents.)
  Solar Charge Controller: PWM-Solar Charge Controller
